// Logisim project project.circ as structural Verilog: 8 circuits, main circuit main
module main (
  output [3:0] out_1
);

  wire CPU_CLOCK_out;
  wire [3:0] INC_sum;

  Clock CPU_CLOCK (.out(CPU_CLOCK_out));
  _4bit_Register PC (.in_1(CPU_CLOCK_out), .in_2(INC_sum), .out_3(out_1));
  _4_bit_adder INC (.in_1(4'b0001), .in_2(out_1), .Sum(INC_sum));  // open: Overflow
endmodule

module _8bit_Register (
  input  clock_input,
  input  [7:0] in_2,
  output [7:0] out_3
);

  D_Flip_Flop d_ff_1 (.clk(clock_input), .D(in_2[6]), .Q(out_3[6]));  // open: Qn, preset, en, reset
  D_Flip_Flop d_ff_2 (.clk(clock_input), .D(in_2[7]), .Q(out_3[7]));  // open: Qn, preset, en, reset
  D_Flip_Flop d_ff_3 (.clk(clock_input), .D(in_2[5]), .Q(out_3[5]));  // open: Qn, preset, en, reset
  D_Flip_Flop d_ff_4 (.clk(clock_input), .D(in_2[4]), .Q(out_3[4]));  // open: Qn, preset, en, reset
  D_Flip_Flop d_ff_5 (.clk(clock_input), .D(in_2[3]), .Q(out_3[3]));  // open: Qn, preset, en, reset
  D_Flip_Flop d_ff_6 (.clk(clock_input), .D(in_2[2]), .Q(out_3[2]));  // open: Qn, preset, en, reset
  D_Flip_Flop d_ff_7 (.clk(clock_input), .D(in_2[1]), .Q(out_3[1]));  // open: Qn, preset, en, reset
  D_Flip_Flop d_ff_8 (.clk(clock_input), .D(in_2[0]), .Q(out_3[0]));  // open: Qn, preset, en, reset
endmodule

module _4bit_Register (
  input  in_1,
  input  [3:0] in_2,
  output [3:0] out_3
);

  D_Flip_Flop d_ff_1 (.clk(in_1), .D(in_2[2]), .Q(out_3[2]));  // open: Qn, preset, en, reset
  D_Flip_Flop d_ff_2 (.clk(in_1), .D(in_2[3]), .Q(out_3[3]));  // open: Qn, preset, en, reset
  D_Flip_Flop d_ff_3 (.clk(in_1), .D(in_2[1]), .Q(out_3[1]));  // open: Qn, preset, en, reset
  D_Flip_Flop d_ff_4 (.clk(in_1), .D(in_2[0]), .Q(out_3[0]));  // open: Qn, preset, en, reset
endmodule

module half_adder (
  input  in_1,
  input  in_2,
  output sum_out,
  output carry_out
);

  xor xor_1 (sum_out, in_1, in_2);
  and and_1 (carry_out, in_1, in_2);
endmodule

module full_adder (
  input  in_1,
  input  in_2,
  input  carry,
  output carry_out,
  output sum_out
);

  wire half_adder_2_carry_out, half_adder_carry_out, half_adder_sum_out;

  half_adder half_adder (.in_1(in_1), .in_2(in_2), .sum_out(half_adder_sum_out), .carry_out(half_adder_carry_out));
  half_adder half_adder_2 (
    .in_1(half_adder_sum_out), .in_2(carry), .sum_out(sum_out), .carry_out(half_adder_2_carry_out));
  or or_1 (carry_out, half_adder_carry_out, half_adder_2_carry_out);
endmodule

module _4_bit_adder (
  input  [3:0] in_1,
  input  [3:0] in_2,
  output Overflow,
  output [3:0] Sum
);

  wire full_adder_1_carry_out, full_adder_3_carry_out, half_adder_1_carry_out;

  half_adder half_adder_1 (.in_1(in_1[0]), .in_2(in_2[0]), .sum_out(Sum[0]), .carry_out(half_adder_1_carry_out));
  full_adder full_adder_1 (
    .in_1(in_1[1]), .in_2(in_2[1]), .carry(half_adder_1_carry_out), .carry_out(full_adder_1_carry_out),
    .sum_out(Sum[1]));
  full_adder full_adder_2 (
    .in_1(in_1[3]), .in_2(in_2[3]), .carry(full_adder_3_carry_out), .carry_out(Overflow), .sum_out(Sum[3]));
  full_adder full_adder_3 (
    .in_1(in_1[2]), .in_2(in_2[2]), .carry(full_adder_1_carry_out), .carry_out(full_adder_3_carry_out),
    .sum_out(Sum[2]));
endmodule

module display (
  input  [7:0] in_1,
  input  in_2,
  output out_3,
  output out_4,
  output out_5,
  output out_6,
  output out_7,
  output out_8,
  output out_9,
  output out_10,
  output out_11,
  output out_12
);

  wire addif5_1_out_6, addif5_1_out_7, addif5_1_out_8, addif5_2_out_6, addif5_2_out_7, addif5_2_out_8,
       addif5_2_out_9, addif5_3_out_6, addif5_3_out_7, addif5_3_out_8, addif5_3_out_9, addif5_5_out_6,
       addif5_5_out_7, addif5_5_out_8, addif5_5_out_9, addif5_6_out_6, addif5_6_out_7, addif5_6_out_8,
       addif5_6_out_9;

  addif5 addif5_1 (
    .in_1(addif5_5_out_9), .in_2(addif5_3_out_9), .in_3(addif5_2_out_9), .in_4(in_2), .out_6(addif5_1_out_6),
    .out_7(addif5_1_out_7), .out_8(addif5_1_out_8), .out_9(out_3));  // open: Overflow
  addif5 addif5_2 (
    .in_1(in_1[5]), .in_2(in_1[6]), .in_3(in_1[7]), .in_4(in_2), .out_6(addif5_2_out_6),
    .out_7(addif5_2_out_7), .out_8(addif5_2_out_8), .out_9(addif5_2_out_9));  // open: Overflow
  addif5 addif5_3 (
    .in_1(in_1[4]), .in_2(addif5_2_out_6), .in_3(addif5_2_out_7), .in_4(addif5_2_out_8),
    .out_6(addif5_3_out_6), .out_7(addif5_3_out_7), .out_8(addif5_3_out_8), .out_9(addif5_3_out_9));  // open: Overflow
  addif5 addif5_4 (
    .in_1(addif5_6_out_9), .in_2(addif5_1_out_6), .in_3(addif5_1_out_7), .in_4(addif5_1_out_8),
    .out_6(out_7), .out_7(out_6), .out_8(out_5), .out_9(out_4));  // open: Overflow
  addif5 addif5_5 (
    .in_1(in_1[3]), .in_2(addif5_3_out_6), .in_3(addif5_3_out_7), .in_4(addif5_3_out_8),
    .out_6(addif5_5_out_6), .out_7(addif5_5_out_7), .out_8(addif5_5_out_8), .out_9(addif5_5_out_9));  // open: Overflow
  addif5 addif5_6 (
    .in_1(in_1[2]), .in_2(addif5_5_out_6), .in_3(addif5_5_out_7), .in_4(addif5_5_out_8),
    .out_6(addif5_6_out_6), .out_7(addif5_6_out_7), .out_8(addif5_6_out_8), .out_9(addif5_6_out_9));  // open: Overflow
  addif5 addif5_7 (
    .in_1(in_1[1]), .in_2(addif5_6_out_6), .in_3(addif5_6_out_7), .in_4(addif5_6_out_8), .out_6(out_11),
    .out_7(out_10), .out_8(out_9), .out_9(out_8));  // open: Overflow

  assign out_12 = in_1[0];
endmodule

module addif5 (
  input  in_1,
  input  in_2,
  input  in_3,
  input  in_4,
  output Overflow,
  output out_6,
  output out_7,
  output out_8,
  output out_9
);

  wire and_1_out, full_adder_1_carry_out, full_adder_2_carry_out, half_adder_1_carry_out, or_1_out, or_2_out;
  wire [3:0] half_adder_1_sum_out;

  or or_1 (or_1_out, in_2, in_1);
  and and_1 (and_1_out, in_3, or_1_out);
  or or_2 (or_2_out, in_4, and_1_out);
  full_adder full_adder_1 (
    .in_1(1'b1), .in_2(in_2), .carry(half_adder_1_carry_out), .carry_out(full_adder_1_carry_out),
    .sum_out(half_adder_1_sum_out[1]));
  half_adder half_adder_1 (
    .in_1(1'b1), .in_2(in_1), .sum_out(half_adder_1_sum_out[0]), .carry_out(half_adder_1_carry_out));
  Multiplexer #(.width(4), .enable("false")) multiplexer_1 (
    .in0({in_4, in_3, in_2, in_1}), .in1(half_adder_1_sum_out), .out({out_9, out_8, out_7, out_6}),
    .sel(or_2_out));
  full_adder full_adder_2 (
    .in_1(1'b0), .in_2(in_3), .carry(full_adder_1_carry_out), .carry_out(full_adder_2_carry_out),
    .sum_out(half_adder_1_sum_out[2]));
  full_adder full_adder_3 (
    .in_1(1'b0), .in_2(in_4), .carry(full_adder_2_carry_out), .carry_out(Overflow),
    .sum_out(half_adder_1_sum_out[3]));
endmodule
